# Fritzing sketch scheme (saved by Fritzing 0.9.3b)
breadboards: 1

parts:
  Lolin_V3_ESP_Board = ESP8266 WiFi Module [part_number=ESP8266]
  PC_USB = USB Connectors [package=usb-a-pcb]

nets:
  N1: Lolin_V3_ESP_Board.VCC, PC_USB.D+
  GND: Lolin_V3_ESP_Board.GND, PC_USB.GND
